// Digital circuit CORE.dig as structural Verilog
module CORE (
  input  clk,
  input  RST,
  input  CLR
);

  wire ALUD_FLAG, ALUD_OE, ALUS_OE, BR_Q, button_1_out, CLK_t, comparator_1_eq, comparator_1_gt,
       comparator_1_lt, d_ff_1_q, DC_JUMP, IMMED_OE, IRQ_OE, PSWF_OE, RAM_OE, RAM_WE, RF_HWE, RF_LWE, ROM_OE,
       RST_t, SR_WE, WR_WE, XRAM_OE;
  wire [2:0] BR_SRC, BUS_SRC, JUMP_TYPE;
  wire [3:0] ALUSD_FUNC, RF_SRC;
  wire [7:0] DBUS, IMMED, RF_Q, SR_q, WR_q;
  wire [11:0] ADDRESS, dcouter_1_q;
  wire [47:42] DECODER_d;

  Button button_1 (.out(button_1_out));
  Comparator #(.Bits(8)) comparator_1 (
    .a(RF_Q), .b(IMMED), .gt(comparator_1_gt), .eq(comparator_1_eq), .lt(comparator_1_lt));
  D_FF d_ff_1 (.D(RST), .C(clk), .Q(d_ff_1_q));  // open: nQ
  DCOUTER dcouter_1 (.CLK(CLK_t), .CLR(CLR), .CNT(1'b1), .LE(DC_JUMP), .D(ADDRESS), .Q(dcouter_1_q));
  Multiplexer #(.Selector_Bits(3)) multiplexer_1 (
    .sel(JUMP_TYPE), .in_0(1'b0), .in_1(1'b1), .in_2(comparator_1_gt), .in_3(comparator_1_eq),
    .in_4(comparator_1_lt), .in_5(BR_Q), .in_6(RST_t), .in_7(1'b0), .out(DC_JUMP));
  // Probe on dcouter_1_q
  ROM #(.AddrBits(12), .Bits(48)) DECODER (
    .A(dcouter_1_q), .sel(1'b1),
    .D({DECODER_d, IMMED, ADDRESS, JUMP_TYPE, ALUSD_FUNC, RAM_WE, BR_SRC, SR_WE, WR_WE, BUS_SRC, RF_HWE, RF_LWE, RF_SRC}));
  D_FF d_ff_2 (.D(d_ff_1_q), .C(clk), .Q(RST_t));  // open: nQ
  // SwitchDT switchdt_1: pin names not known; wires that end beside it: clk, button_1_out, CLK_t
  Decoder #(.Selector_Bits(3)) decoder_2 (
    .sel(BUS_SRC), .out_0(PSWF_OE), .out_1(ALUS_OE), .out_2(ALUD_OE), .out_3(IMMED_OE), .out_4(RAM_OE),
    .out_5(XRAM_OE), .out_6(ROM_OE), .out_7(IRQ_OE));
  // Probe RF_SRC on RF_SRC
  // Probe on RF_LWE
  // Probe on RF_HWE
  // Probe on BUS_SRC
  // Probe on WR_WE
  // Probe on SR_WE
  // Probe on BR_SRC
  // Probe on RAM_WE
  // Probe on ALUSD_FUNC
  // Probe on JUMP_TYPE
  // Probe on ADDRESS
  // Probe on IMMED
  // Probe on DBUS
  PullDown #(.Bits(8)) pulldown_1 (.out(DBUS));
  // reg_file RF: pin names not known; wires that end beside it: CLK_t, RF_SRC, DBUS, RF_LWE, RF_HWE, RF_Q
  // Probe on RF_Q
  BR BR (
    .CLK(CLK_t), .CLR(CLR), .S(BR_SRC), .ALUDF(ALUD_FLAG), .ALUSF(ALUD_FLAG), .A0(RF_Q[0]), .A7(RF_Q[7]),
    .Q(BR_Q));
  reg8clr WR (.D(DBUS), .CLK(CLK_t), .CLR(CLR), .LE(WR_WE), .Q(WR_q));
  reg8clr SR (.D(DBUS), .CLK(CLK_t), .CLR(CLR), .LE(SR_WE), .Q(SR_q));
  // Probe on WR_q
  // Probe on SR_q
  // Probe on {SR_q, WR_q}
  assign DBUS = IMMED_OE ? IMMED : 8'bz;  // Driver driver_1
  ALU ALU (
    .A(RF_Q), .B(WR_q), .S(ALUSD_FUNC), .CI(BR_Q), .nSOE(ALUS_OE), .nDLOE(ALUD_OE), .nDHOE(PSWF_OE),
    .O(DBUS), .CO(ALUD_FLAG));
  ROM #(.AddrBits(16), .Bits(8)) ROM (.A({SR_q, WR_q}), .sel(ROM_OE), .D(DBUS));
  RAMSinglePortSel #(.AddrBits(7), .Bits(8)) RAM (.A(SR_q[6:0]), .CS(SR_q[7]), .WE(RAM_WE), .OE(RAM_OE), .D(DBUS));

  // Notes on the sheet:
  //   clk: Hz: 500
  //   contents of DECODER (hex, n*v repeats v):
  //   4cf02880,18073,248,449,1ba,1ac0,2a8b8,290b9,2002220000a,30012e0000a,3800ae0000a,3c006e0000a,
  //   3e00520000a,3f00460000a,3f80420000a,3fc0420000a,3f40460000a,3e804e0000a,3ec04e0000a,
  //   3e40520000a,3d00620000a,3d805e0000a,3dc05e0000a,3d40620000a,3c806a0000a,3cc06a0000a,
  //   3c406e0000a,3a008e0000a,3b00820000a,3b807e0000a,3bc07e0000a,3b40820000a,3a808a0000a,
  //   3ac08a0000a,3a408e0000a,39009e0000a,39809a0000a,39c09a0000a,39409e0000a,3880a60000a,
  //   38c0a60000a,3840ae0000a,45c80248,3400ee0000a,3600d20000a,3700c60000a,3780c20000a,
  //   37c0c20000a,3740c60000a,3680ce0000a,36c0ce0000a,3640d20000a,3500e20000a,3580de0000a,
  //   35c0de0000a,3540e20000a,3480ea0000a,34c0ea0000a,3440ee0000a,32010e0000a,3301020000a,
  //   3380fe0000a,33c0fe0000a,3341020000a,32810a0000a,32c10a0000a,32410e0000a,31011e0000a,
  //   31811a0000a,31c11a0000a,31411e0000a,3081260000a,30c1260000a,30412e0000a,45c80248,
  //   2801c20000a,2c01720000a,2e01560000a,2f014a0000a,2f81460000a,2fc1460000a,2f414a0000a,
  //   2e81520000a,2ec1520000a,2e41560000a,2d01660000a,2d81620000a,2dc1620000a,2d41660000a,
  //   2c816e0000a,2cc16e0000a,2c41720000a,2a01920000a,2b01860000a,2b81820000a,2bc1820000a,
  //   2b41860000a,2a818e0000a,2ac18e0000a,2a41920000a,2901a20000a,29819e0000a,29c19e0000a,
  //   2941a20000a,2881ba0000a,28c1ba0000a,10c0,2a834,29035,47880000,2841c20000a,45c80248,
  //   2401e20000a,2601ca0000a,2501d60000a,2581d20000a,2541d60000a,2481de0000a,24c1de0000a,
  //   2441e20000a,2202020000a,2301f60000a,2381f20000a,23c1f20000a,2341f60000a,2281fe0000a,
  //   22c1fe0000a,2242020000a,2102120000a,21820e0000a,21c20e0000a,2142120000a,20821a0000a,
  //   20c21a0000a,2042220000a,45c80248,1003420000a,1802c20000a,1c02820000a,1e024e0000a,
  //   1f02420000a,1f823e0000a,1fc23e0000a,1f42420000a,1e824a0000a,1ec24a0000a,1e424e0000a,
  //   1d02760000a,1d825a0000a,1dc25a0000a,1d425e0000a,248,449,1b0,1ac0,2a8b8,478a90b9,1c827e0000a,
  //   1cc27e0000a,1c42820000a,1a02a20000a,1b02960000a,1b82920000a,1bc2920000a,1b42960000a,
  //   1a829e0000a,1ac29e0000a,1a42a20000a,1902b20000a,1982ae0000a,19c2ae0000a,1942b20000a,
  //   1882ba0000a,18c2ba0000a,1842c20000a,45c80248,1403020000a,1602e60000a,1702da0000a,
  //   1782d60000a,17c2d60000a,1742da0000a,1682e20000a,16c2e20000a,1642e60000a,1502f60000a,
  //   1582f20000a,15c2f20000a,1542f60000a,1482fe0000a,14c2fe0000a,1443020000a,1203220000a,
  //   1303160000a,1383120000a,13c3120000a,1343160000a,12831e0000a,12c31e0000a,1243220000a,
  //   1103320000a,11832e0000a,11c32e0000a,1143320000a,10833a0000a,10c33a0000a,1043420000a,
  //   45c80248,803c60000a,c03860000a,e036a0000a,f035e0000a,f835a0000a,fc35a0000a,f435e0000a,
  //   e83660000a,ec3660000a,e436a0000a,d037a0000a,d83760000a,dc3760000a,d437a0000a,c83820000a,
  //   cc3820000a,c43860000a,a03a60000a,b039a0000a,b83960000a,bc3960000a,b439a0000a,a83a20000a,
  //   ac3a20000a,a43a60000a,903b60000a,983b20000a,9c3b20000a,943b60000a,883c20000a,8c3c20000a,
  //   45c80248,843c60000a,404060000a,603ea0000a,703de0000a,783da0000a,7c3da0000a,743de0000a,
  //   683e60000a,6c3e60000a,643ea0000a,503fa0000a,583f60000a,5c3f60000a,543fa0000a,484020000a,
  //   4c4020000a,444060000a,204260000a,3041a0000a,384160000a,3c4160000a,3441a0000a,284220000a,
  //   2c4220000a,244260000a,1043a0000a,184320000a,1c4320000a,144360000a,40070,84560000a,
  //   c4460000a,20070,278,478,1bc,478801bc,447a0000a,248,449,1bc,2a838,2a839,24c,180b8,
  //   24a,200002003c6,1803c,40020000c,400bc,24b,180bd,180be,402bd,124c,3280d,4aa80000,80000,
  //   482bc,100000,40472,4048,40472,4049,c000002c0,200bc,980b8,f0,f1,f2,f3,f4,f5,f6,f7,
  //   f8,f9,fa,4cf000fb,80000
  //   contents of ROM (hex, n*v repeats v):
  //   74,0,74,1,74,2,74,3,74,4,74,5,74,6,74,7,74,8,74,9,74,a,74,b,74,c,74,d,74,e,74,f,74,
  //   10,74,11,74,12,74,13,74,14,74,15,74,16,74,17,74,18,74,19,74,1a,74,1b,74,1c,74,1d,
  //   74,1e,74,1f,74,20,74,21,74,22,74,23,74,24,74,25,74,26,74,27,74,28,74,29,74,2a,74,
  //   2b,74,2c,74,2d,74,2e,74,2f,74,30,74,31,74,32,74,33,74,34,74,35,74,36,74,37,74,38,
  //   74,39,74,3a,74,3b,74,3c,74,3d,74,3e,74,3f,74,40,74,41,74,42,74,43,74,44,74,45,74,
  //   46,74,47,74,48,74,49,74,4a,74,4b,74,4c,74,4d,74,4e,74,4f,74,50,74,51,74,52,74,53,
  //   74,54,74,55,74,56,74,57,74,58,74,59,74,5a,74,5b,74,5c,74,5d,74,5e,74,5f,74,60,74,
  //   61,74,62,74,63,74,64,74,65,74,66,74,67,74,68,74,69,74,6a,74,6b,74,6c,74,6d,74,6e,
  //   74,6f,74,70,74,71,74,72,74,73,74,74,74,75,74,76,74,77,74,78,74,79,74,7a,74,7b,74,
  //   7c,74,7d,74,7e,74,7f,74,80,74,81,74,82,74,83,74,84,74,85,74,86,74,87,74,88,74,89,
  //   74,8a,74,8b,74,8c,74,8d,74,8e,74,8f,74,90,74,91,74,92,74,93,74,94,74,95,74,96,74,
  //   97,74,98,74,99,74,9a,74,9b,74,9c,74,9d,74,9e,74,9f,74,a0,74,a1,74,a2,74,a3,74,a4,
  //   74,a5,74,a6,74,a7,74,a8,74,a9,74,aa,74,ab,74,ac,74,ad,74,ae,74,af,74,b0,74,b1,74,
  //   b2,74,b3,74,b4,74,b5,74,b6,74,b7,74,b8,74,b9,74,ba,74,bb,74,bc,74,bd,74,be,74,bf,
  //   74,c0,74,c1,74,c2,74,c3,74,c4,74,c5,74,c6,74,c7,74,c8,74,c9,74,ca,74,cb,74,cc,74,
  //   cd,74,ce,74,cf,74,d0,74,d1,74,d2,74,d3,74,d4,74,d5,74,d6,74,d7,74,d8,74,d9,74,da,
  //   74,db,74,dc,74,dd,74,de,74,df,74,e0,74,e1,74,e2,74,e3,74,e4,74,e5,74,e6,74,e7,74,
  //   e8,74,e9,74,ea,74,eb,74,ec,74,ed,74,ee,74,ef,74,f0,74,f1,74,f2,74,f3,74,f4,74,f5,
  //   74,f6,74,f7,74,f8,74,f9,74,fa,74,fb,74,fc,74,fd,74,fe,74,ff
endmodule
